// Logisim project PyGO.circ as structural Verilog: 12 circuits, main circuit PROCESSADOR
// Py-Go
module PROCESSADOR (
  output [31:0] \INSTRUÇÃO 
);

  wire Clock, data_razard_1, data_razard_2, Inst_reset, J, Jc, Li_1, Li_2, li_r_1, li_r_2, marc, Mem_reset,
       mine1_out, mine2_out, not_1_out, T_or_F, writ_reg_1, writ_reg_2;
  wire [5:0] pipeline_2_1_out_14, pipeline_3_1_out_11, pipeline_3_1_out_17, pipeline_4_1_out_10;
  wire [7:0] UC_sp2, UC_ula_op;
  wire [15:0] pipeline_2_1_out_9;
  wire [31:0] adder_1_out, auxiliar_do_branch_1_out_5, banco_de_registradores_1_r1_d, \Instrução_2 ,
       \Instrução_2_1 , \Instrução_2_2 , memoriadados_1_out_7, memoriainstrucoes_1_out_2, multiplexer_1_out,
       multiplexer_2_out, multiplexer_3_out, multiplexer_4_out, multiplexer_6_out, PC_q, pipeline_1_1_out_6,
       pipeline_1_1_out_8, pipeline_2_1_out_10, pipeline_2_1_out_11, pipeline_2_1_out_12,
       pipeline_2_1_out_13, pipeline_3_1_out_12, pipeline_3_1_out_13, pipeline_3_1_out_14,
       pipeline_3_1_out_15, pipeline_3_1_out_16, pipeline_4_1_out_8, pipeline_4_1_out_9, R0D, R2D, R2D_1,
       R3D, R3D_1, redutor_1_out_2, register_1_q, register_3_q, register_7_q, register_8_q, ULA_1,
       ula_1_ula_out, ULA_2, ULA_Res_2;

  Multiplexer #(.width(32), .enable("false")) multiplexer_1 (
    .in0(adder_1_out), .in1(pipeline_3_1_out_12), .out(multiplexer_1_out), .sel(marc));
  Clock clock_1 (.out(Clock));
  Button button_1 (.out(Inst_reset));
  Button button_2 (.out(Mem_reset));
  Register #(.width(32)) PC (.D(multiplexer_1_out), .Q(PC_q), .clk(Clock), .clr(Inst_reset));  // open: en
  Adder #(.width(32)) adder_1 (.a(32'h4), .b(PC_q), .out(adder_1_out));  // open: cin, cout
  MemoriaInstrucoes memoriainstrucoes_1 (.out_2(memoriainstrucoes_1_out_2), .out_3(\Instrução_2 ), .in_1(PC_q[9:2]));
  Register #(.width(32)) register_1 (.D(\Instrução_2 ), .Q(register_1_q), .clk(Clock), .clr(Inst_reset));  // open: en
  Pipeline_1 pipeline_1_1 (
    .in_1(adder_1_out), .in_2(memoriainstrucoes_1_out_2), .in_3(\Instrução_2 ), .in_4(Clock),
    .out_6(pipeline_1_1_out_6), .out_7(\INSTRUÇÃO ), .out_8(pipeline_1_1_out_8), .in_5(Inst_reset));
  Register #(.width(32)) register_2 (.D(register_1_q), .Q(\Instrução_2_1 ), .clk(Clock), .clr(Inst_reset));  // open: en
  UC UC (
    .E3(\INSTRUÇÃO [31]), .E2(\INSTRUÇÃO [30]), .ula_op(UC_ula_op[0]), .E1(\INSTRUÇÃO [29]),
    .E0(\INSTRUÇÃO [28]), .ula_r(UC_ula_op[1]), .write_reg(UC_ula_op[2]), .li(UC_ula_op[3]),
    .j(UC_ula_op[4]), .branch(UC_ula_op[5]), .MemRead(UC_ula_op[6]), .MemWrite(UC_ula_op[7]),
    .datarazard_1(data_razard_1), .EP2(pipeline_1_1_out_8[31:28]), .SP2(UC_sp2), .datarazard_2(data_razard_2));
  BANCO_DE_REGISTRADORES banco_de_registradores_1 (
    .DATA_WRITE(multiplexer_3_out), .CLK(Clock), .RW1(pipeline_4_1_out_10[2:0]), .R0_D(R0D),
    .R0(\INSTRUÇÃO [19:16]), .R1_D(banco_de_registradores_1_r1_d), .R1(\INSTRUÇÃO [23:20]),
    .RESET(Inst_reset), .R2_D(R2D), .R2(pipeline_1_1_out_8[19:16]), .R3_D(R3D),
    .R3(pipeline_1_1_out_8[23:20]), .RW2_2(writ_reg_2), .RW2(pipeline_4_1_out_10[5:3]), .RW1_2(writ_reg_1),
    .DATA_WRITE_2(ULA_Res_2));
  Register #(.width(32)) register_3 (.D(\Instrução_2_1 ), .Q(register_3_q), .clk(Clock), .clr(Inst_reset));  // open: en
  Register #(.width(32)) register_4 (.D(register_3_q), .Q(\Instrução_2_2 ), .clk(Clock), .clr(Inst_reset));  // open: en
  Multiplexer #(.width(32), .enable("false")) multiplexer_2 (
    .in0(R0D), .in1(ULA_1), .out(multiplexer_2_out), .sel(data_razard_1));
  Multiplexer #(.width(32), .enable("false")) multiplexer_3 (
    .in0(pipeline_4_1_out_9), .in1({{8{1'b0}}, pipeline_4_1_out_8[23:0]}), .out(multiplexer_3_out), .sel(Li_1));
  Multiplexer #(.width(32), .enable("false")) multiplexer_4 (
    .in0(R2D), .in1(ULA_2), .out(multiplexer_4_out), .sel(data_razard_2));
  Pipeline_2 pipeline_2_1 (
    .in_1({UC_sp2, UC_ula_op}), .in_2(\INSTRUÇÃO ), .in_3(\INSTRUÇÃO ), .in_4(multiplexer_2_out),
    .in_5(banco_de_registradores_1_r1_d), .in_6({pipeline_1_1_out_8[26:24], \INSTRUÇÃO [26:24]}),
    .in_7(Clock),
    .out_9({pipeline_2_1_out_9[15:12], li_r_2, pipeline_2_1_out_9[10:5], J, li_r_1, pipeline_2_1_out_9[2:0]}),
    .out_10(pipeline_2_1_out_10), .out_11(pipeline_2_1_out_11), .out_12(pipeline_2_1_out_12),
    .out_13(pipeline_2_1_out_13), .out_14(pipeline_2_1_out_14), .in_8(Inst_reset));
  Register #(.width(32)) register_5 (.D(multiplexer_4_out), .Q(R2D_1), .clk(Clock), .clr(Inst_reset));  // open: en
  Register #(.width(32)) register_6 (.D(R3D), .Q(R3D_1), .clk(Clock), .clr(Inst_reset));  // open: en
  auxiliar_do_branch auxiliar_do_branch_1 (
    .Normal(pipeline_1_1_out_6), .Sem_soma(pipeline_2_1_out_11), .in_3(Jc), .j(J),
    .out_5(auxiliar_do_branch_1_out_5));
  and and_1 (Jc, pipeline_2_1_out_9[5], T_or_F);
  ULA u_ula_1 (
    .DATA_0_1(pipeline_2_1_out_12), .DATA_1_1(pipeline_2_1_out_13), .ULA_OUT(ula_1_ula_out), .out_8(T_or_F),
    .clk(Clock), .DATA_0_2(R2D_1), .ULA_OUT_2(ULA_2), .DATA_1_2(R3D_1),
    .ULA_OP({pipeline_2_1_out_9[9:8], pipeline_2_1_out_9[1:0]}));
  REDUTOR redutor_1 (.out_2(redutor_1_out_2), .in_1(pipeline_2_1_out_10));
  Multiplexer #(.width(32), .enable("false")) multiplexer_5 (
    .in0(redutor_1_out_2), .in1(ula_1_ula_out), .out(ULA_1), .sel(not_1_out));
  not not_1 (not_1_out, li_r_1);
  or mine1 (mine1_out, Jc, J);
  Pipeline_3 pipeline_3_1 (
    .in_1({pipeline_2_1_out_9[7:6], li_r_2, li_r_1, pipeline_2_1_out_9[10], pipeline_2_1_out_9[2]}),
    .in_2(auxiliar_do_branch_1_out_5), .in_3(pipeline_2_1_out_10), .in_4(pipeline_2_1_out_12),
    .in_5(ula_1_ula_out), .in_6(pipeline_2_1_out_13), .in_7(pipeline_2_1_out_14), .in_8(mine1_out),
    .in_9(Clock), .out_11(pipeline_3_1_out_11), .out_12(pipeline_3_1_out_12), .out_13(pipeline_3_1_out_13),
    .out_14(pipeline_3_1_out_14), .out_15(pipeline_3_1_out_15), .out_16(pipeline_3_1_out_16),
    .out_17(pipeline_3_1_out_17), .out_18(marc), .in_10(Inst_reset));
  Register #(.width(32)) register_7 (.D(ULA_2), .Q(register_7_q), .clk(Clock), .clr(Inst_reset));  // open: en
  Register #(.width(32)) register_8 (.D(register_7_q), .Q(register_8_q), .clk(Clock), .clr(Inst_reset));  // open: en
  Multiplexer #(.width(32), .enable("false")) multiplexer_6 (
    .in0(pipeline_3_1_out_14), .in1(pipeline_3_1_out_15), .out(multiplexer_6_out), .sel(mine2_out));
  nor mine2 (mine2_out, pipeline_3_1_out_11[5], pipeline_3_1_out_11[4]);
  Multiplexer #(.width(32), .enable("false")) multiplexer_7 (
    .in0(register_8_q), .in1({{8{1'b0}}, \Instrução_2_2 [23:0]}), .out(ULA_Res_2), .sel(Li_2));
  MemoriaDados memoriadados_1 (
    .in_1(multiplexer_6_out), .in_3(pipeline_3_1_out_16), .MemWrite(pipeline_3_1_out_11[5]),
    .out_7(memoriadados_1_out_7), .clk(Clock), .MemRead(pipeline_3_1_out_11[4]), .limpa(Mem_reset));
  Pipeline_4 pipeline_4_1 (
    .in_1(pipeline_3_1_out_11[3:0]), .in_2(pipeline_3_1_out_13), .in_3(memoriadados_1_out_7),
    .in_4(pipeline_3_1_out_17), .in_5(Clock), .out_7({Li_2, Li_1, writ_reg_2, writ_reg_1}),
    .out_8(pipeline_4_1_out_8), .out_9(pipeline_4_1_out_9), .out_10(pipeline_4_1_out_10), .in_6(Inst_reset));

  // Notes on the sheet:
  //   REG_0
  //   REG_1
  //   REG_W
  //   DATA_W
  //   REG_1
  //   REG_W
  //   BANCO DE REGISTRADORES
  //   REG0_D
  //   ULA
endmodule

module ULA (
  input  [31:0] DATA_0_1,
  input  [31:0] DATA_1_1,
  input  clk,
  input  [3:0] ULA_OP,
  input  [31:0] DATA_0_2,
  input  [31:0] DATA_1_2,
  output [31:0] ULA_OUT,
  output out_8,
  output [31:0] ULA_OUT_2
);

  wire comparator_1_eq, comparator_1_gt, comparator_1_lt;
  wire [6:0] random_1_out, random_2_out;
  wire [31:0] adder_1_out, adder_2_out, multiplier_1_out, multiplier_2_out, subtractor_1_out,
       subtractor_2_out;

  Adder #(.width(32)) adder_1 (.a(DATA_0_1), .b(DATA_1_1), .out(adder_1_out));  // open: cin, cout
  Subtractor #(.width(32)) subtractor_1 (.a(DATA_0_1), .b(DATA_1_1), .out(subtractor_1_out));  // open: bin, bout
  Multiplier #(.width(32)) multiplier_1 (.a(DATA_0_1), .b(DATA_1_1), .out(multiplier_1_out));  // open: cin, cout
  Comparator #(.width(32), .mode("unsigned")) comparator_1 (
    .a(DATA_0_1), .b(DATA_1_1), .gt(comparator_1_gt), .eq(comparator_1_eq), .lt(comparator_1_lt));
  Random #(.width(7)) random_1 (.clk(clk), .out(random_1_out));  // open: next, clr
  Adder #(.width(32)) adder_2 (.a(DATA_0_2), .b(DATA_1_2), .out(adder_2_out));  // open: cin, cout
  Subtractor #(.width(32)) subtractor_2 (.a(DATA_0_2), .b(DATA_1_2), .out(subtractor_2_out));  // open: bin, bout
  Multiplier #(.width(32)) multiplier_2 (.a(DATA_0_2), .b(DATA_1_2), .out(multiplier_2_out));  // open: cin, cout
  Random #(.width(7), .trigger("falling")) random_2 (.clk(clk), .out(random_2_out));  // open: next, clr
  Multiplexer #(.select(2), .width(32), .enable("false")) multiplexer_1 (
    .in0(adder_1_out), .in1(subtractor_1_out), .in2(multiplier_1_out), .in3({{25{1'b0}}, random_1_out}),
    .out(ULA_OUT), .sel(ULA_OP[1:0]));
  Multiplexer #(.select(2), .width(32), .enable("false")) multiplexer_2 (
    .in0(adder_2_out), .in1(subtractor_2_out), .in2(multiplier_2_out), .in3({{25{1'b0}}, random_2_out}),
    .out(ULA_OUT_2), .sel(ULA_OP[3:2]));
  Multiplexer #(.select(2), .enable("false")) multiplexer_3 (
    .in0(comparator_1_gt), .in1(comparator_1_eq), .in2(comparator_1_lt), .in3(1'b0), .out(out_8),
    .sel(ULA_OP[1:0]));

  // Other names for the same wires on the sheet: c = clk
endmodule

module UC (
  input  E3,
  input  E2,
  input  [3:0] EP2,
  input  E1,
  input  E0,
  output ula_op,
  output [7:0] SP2,
  output ula_r,
  output write_reg,
  output li,
  output j,
  output branch,
  output MemRead,
  output MemWrite,
  output datarazard_1,
  output datarazard_2
);

  wire and_1_out, and_2_out, and_3_out, and_4_out, and_5_out, and_6_out, and_7_out, and_9_out, and_10_out,
       and_11_out, and_12_out, and_13_out, and_14_out, and_15_out, and_18_out, and_19_out, and_20_out,
       and_21_out, and_23_out, and_24_out, and_25_out, and_26_out, and_27_out, and_28_out, and_29_out,
       and_30_out, and_31_out, and_32_out, and_33_out, and_34_out, and_37_out, and_38_out, and_39_out,
       and_40_out, and_41_out, and_42_out, not_1_out, not_2_out, not_3_out, not_4_out, not_5_out, not_6_out,
       not_7_out, not_8_out, not_9_out, not_10_out, not_11_out, not_12_out, not_13_out, not_14_out,
       not_15_out, not_16_out, not_17_out, not_18_out, not_19_out, not_20_out, not_21_out, not_22_out,
       not_23_out, not_24_out, not_25_out, not_26_out, not_27_out, not_28_out, not_29_out, not_30_out,
       not_31_out, not_32_out, not_33_out, not_34_out, not_35_out, not_36_out, not_37_out, not_38_out,
       not_39_out, not_40_out, not_41_out, not_42_out, not_43_out, not_44_out, not_45_out, not_46_out,
       not_47_out, not_48_out, not_49_out, not_50_out, not_51_out, not_52_out, not_53_out, not_54_out,
       not_55_out, not_56_out, not_57_out, not_58_out, not_59_out, not_60_out, not_61_out, not_62_out,
       not_63_out, not_64_out, not_65_out, not_66_out, not_67_out, not_68_out, not_69_out, not_70_out;

  not not_1 (not_1_out, E2);
  not not_2 (not_2_out, E1);
  not not_3 (not_3_out, E3);
  not not_4 (not_4_out, E0);
  not not_5 (not_5_out, E2);
  not not_6 (not_6_out, E0);
  not not_7 (not_7_out, E3);
  not not_8 (not_8_out, E1);
  not not_9 (not_9_out, E0);
  not not_10 (not_10_out, E3);
  not not_11 (not_11_out, E2);
  not not_12 (not_12_out, E0);
  not not_13 (not_13_out, E1);
  not not_14 (not_14_out, E3);
  and and_1 (and_1_out, not_14_out, not_15_out, not_16_out);
  not not_15 (not_15_out, E2);
  not not_16 (not_16_out, E1);
  not not_17 (not_17_out, E2);
  and and_2 (and_2_out, not_17_out, not_18_out);
  not not_18 (not_18_out, E0);
  not not_19 (not_19_out, E1);
  and and_3 (and_3_out, not_19_out, not_20_out);
  not not_20 (not_20_out, E0);
  and and_4 (and_4_out, E3, not_21_out);
  not not_21 (not_21_out, E0);
  and and_5 (and_5_out, E3, E2, not_22_out);
  not not_22 (not_22_out, E1);
  not not_23 (not_23_out, E3);
  not not_24 (not_24_out, E2);
  not not_25 (not_25_out, E0);
  not not_26 (not_26_out, E3);
  not not_27 (not_27_out, E2);
  not not_28 (not_28_out, E3);
  and and_6 (and_6_out, not_28_out, E2, E0);
  not not_29 (not_29_out, E3);
  and and_7 (and_7_out, not_29_out, E2, E1);
  not not_30 (not_30_out, E2);
  not not_31 (not_31_out, E1);
  not not_32 (not_32_out, E0);
  not not_33 (not_33_out, E0);
  not not_34 (not_34_out, E2);
  not not_35 (not_35_out, E1);
  and and_8 (datarazard_1, E3, E2);
  and and_9 (and_9_out, not_1_out, not_2_out, E0);
  or or_1 (ula_op, and_9_out, and_10_out, and_11_out);
  and and_10 (and_10_out, not_3_out, E2, E1, not_4_out);
  and and_11 (and_11_out, E3, not_5_out, E1, not_6_out);
  and and_12 (and_12_out, not_7_out, E2, not_8_out, not_9_out);
  and and_13 (and_13_out, not_10_out, E2, E1, E0);
  and and_14 (and_14_out, E3, not_11_out, E1, not_12_out);
  and and_15 (and_15_out, E3, E2, not_13_out, E0);
  or or_2 (write_reg, and_1_out, and_2_out, and_3_out, and_4_out, and_5_out);
  and and_16 (li, not_23_out, not_24_out, E1, not_25_out);
  and and_17 (j, not_26_out, not_27_out, E1, E0);
  or or_3 (branch, and_6_out, and_7_out);
  and and_18 (and_18_out, E3, not_30_out, not_31_out, not_32_out);
  or or_4 (MemRead, and_18_out, and_19_out);
  and and_19 (and_19_out, E3, E2, E1, not_33_out);
  and and_20 (and_20_out, E3, not_34_out, not_35_out, E0);
  or or_5 (MemWrite, and_20_out, and_21_out);
  and and_21 (and_21_out, E3, E2, E1, E0);
  or or_6 (ula_r, and_12_out, and_13_out, and_14_out, and_15_out);
  not not_36 (not_36_out, EP2[2]);
  not not_37 (not_37_out, EP2[1]);
  not not_38 (not_38_out, EP2[3]);
  not not_39 (not_39_out, EP2[0]);
  not not_40 (not_40_out, EP2[2]);
  not not_41 (not_41_out, EP2[0]);
  not not_42 (not_42_out, EP2[3]);
  not not_43 (not_43_out, EP2[1]);
  not not_44 (not_44_out, EP2[0]);
  not not_45 (not_45_out, EP2[3]);
  not not_46 (not_46_out, EP2[2]);
  not not_47 (not_47_out, EP2[0]);
  not not_48 (not_48_out, EP2[1]);
  not not_49 (not_49_out, EP2[3]);
  not not_50 (not_50_out, EP2[2]);
  not not_51 (not_51_out, EP2[1]);
  not not_52 (not_52_out, EP2[2]);
  not not_53 (not_53_out, EP2[0]);
  not not_54 (not_54_out, EP2[1]);
  not not_55 (not_55_out, EP2[0]);
  not not_56 (not_56_out, EP2[0]);
  not not_57 (not_57_out, EP2[1]);
  not not_58 (not_58_out, EP2[3]);
  not not_59 (not_59_out, EP2[2]);
  not not_60 (not_60_out, EP2[0]);
  not not_61 (not_61_out, EP2[3]);
  not not_62 (not_62_out, EP2[2]);
  not not_63 (not_63_out, EP2[3]);
  not not_64 (not_64_out, EP2[3]);
  not not_65 (not_65_out, EP2[2]);
  not not_66 (not_66_out, EP2[1]);
  not not_67 (not_67_out, EP2[0]);
  not not_68 (not_68_out, EP2[0]);
  not not_69 (not_69_out, EP2[2]);
  not not_70 (not_70_out, EP2[1]);
  and and_22 (datarazard_2, EP2[3], EP2[2]);
  and and_23 (and_23_out, not_36_out, not_37_out, EP2[0]);
  and and_24 (and_24_out, not_38_out, EP2[2], EP2[1], not_39_out);
  and and_25 (and_25_out, EP2[3], not_40_out, EP2[1], not_41_out);
  and and_26 (and_26_out, not_42_out, EP2[2], not_43_out, not_44_out);
  and and_27 (and_27_out, not_45_out, EP2[2], EP2[1], EP2[0]);
  and and_28 (and_28_out, EP2[3], not_46_out, EP2[1], not_47_out);
  and and_29 (and_29_out, EP2[3], EP2[2], not_48_out, EP2[0]);
  and and_30 (and_30_out, not_49_out, not_50_out, not_51_out);
  and and_31 (and_31_out, not_52_out, not_53_out);
  and and_32 (and_32_out, not_54_out, not_55_out);
  and and_33 (and_33_out, EP2[3], not_56_out);
  and and_34 (and_34_out, EP2[3], EP2[2], not_57_out);
  and and_35 (SP2[3], not_58_out, not_59_out, EP2[1], not_60_out);
  and and_36 (SP2[4], not_61_out, not_62_out, EP2[1], EP2[0]);
  and and_37 (and_37_out, not_63_out, EP2[2], EP2[0]);
  and and_38 (and_38_out, not_64_out, EP2[2], EP2[1]);
  and and_39 (and_39_out, EP2[3], not_65_out, not_66_out, not_67_out);
  and and_40 (and_40_out, EP2[3], EP2[2], EP2[1], not_68_out);
  and and_41 (and_41_out, EP2[3], not_69_out, not_70_out, EP2[0]);
  and and_42 (and_42_out, EP2[3], EP2[2], EP2[1], EP2[0]);
  or or_7 (SP2[0], and_23_out, and_24_out, and_25_out);
  or or_8 (SP2[1], and_26_out, and_27_out, and_28_out, and_29_out);
  or or_9 (SP2[2], and_30_out, and_31_out, and_32_out, and_33_out, and_34_out);
  or or_10 (SP2[5], and_37_out, and_38_out);
  or or_11 (SP2[6], and_39_out, and_40_out);
  or or_12 (SP2[7], and_41_out, and_42_out);
endmodule

module BANCO_DE_REGISTRADORES (
  input  [31:0] DATA_WRITE,
  input  [3:0] R0,
  input  [3:0] R1,
  input  [3:0] R2,
  input  [3:0] R3,
  input  [31:0] DATA_WRITE_2,
  input  CLK,
  input  RESET,
  input  [2:0] RW1,
  input  [2:0] RW2,
  input  RW1_2,
  input  RW2_2,
  output [31:0] R0_D,
  output [31:0] R1_D,
  output [31:0] R2_D,
  output [31:0] R3_D
);

  wire demultiplexer_1_out0, demultiplexer_1_out1, demultiplexer_1_out2, demultiplexer_1_out3,
       demultiplexer_1_out4, demultiplexer_1_out5, demultiplexer_1_out6, demultiplexer_1_out7,
       demultiplexer_2_out0, demultiplexer_2_out1, demultiplexer_2_out2, demultiplexer_2_out3,
       demultiplexer_2_out4, demultiplexer_2_out5, demultiplexer_2_out6, demultiplexer_2_out7;
  wire [31:0] register_1_q, register_2_q, register_3_q, register_4_q, register_5_q, register_6_q,
       register_7_q, register_8_q, register_9_q, register_10_q, register_11_q, register_12_q, register_13_q,
       register_14_q, register_15_q, register_16_q;

  Demultiplexer #(.select(3)) demultiplexer_1 (
    .out0(demultiplexer_1_out0), .out1(demultiplexer_1_out1), .out2(demultiplexer_1_out2),
    .out3(demultiplexer_1_out3), .out4(demultiplexer_1_out4), .out5(demultiplexer_1_out5),
    .out6(demultiplexer_1_out6), .out7(demultiplexer_1_out7), .in(RW1_2), .sel(RW1));  // open: en
  Demultiplexer #(.select(3)) demultiplexer_2 (
    .out0(demultiplexer_2_out0), .out1(demultiplexer_2_out1), .out2(demultiplexer_2_out2),
    .out3(demultiplexer_2_out3), .out4(demultiplexer_2_out4), .out5(demultiplexer_2_out5),
    .out6(demultiplexer_2_out6), .out7(demultiplexer_2_out7), .in(RW2_2), .sel(RW2));  // open: en
  Register #(.width(32)) register_1 (
    .D(DATA_WRITE), .en(demultiplexer_1_out0), .Q(register_1_q), .clk(CLK), .clr(RESET));
  Register #(.width(32)) register_2 (
    .D(DATA_WRITE), .en(demultiplexer_1_out1), .Q(register_2_q), .clk(CLK), .clr(RESET));
  Register #(.width(32)) register_3 (
    .D(DATA_WRITE), .en(demultiplexer_1_out2), .Q(register_3_q), .clk(CLK), .clr(RESET));
  Register #(.width(32)) register_4 (
    .D(DATA_WRITE), .en(demultiplexer_1_out3), .Q(register_4_q), .clk(CLK), .clr(RESET));
  Register #(.width(32)) register_5 (
    .D(DATA_WRITE), .en(demultiplexer_1_out4), .Q(register_5_q), .clk(CLK), .clr(RESET));
  Register #(.width(32)) register_6 (
    .D(DATA_WRITE), .en(demultiplexer_1_out5), .Q(register_6_q), .clk(CLK), .clr(RESET));
  Register #(.width(32)) register_7 (
    .D(DATA_WRITE), .en(demultiplexer_1_out6), .Q(register_7_q), .clk(CLK), .clr(RESET));
  Register #(.width(32)) register_8 (
    .D(DATA_WRITE), .en(demultiplexer_1_out7), .Q(register_8_q), .clk(CLK), .clr(RESET));
  Register #(.width(32)) register_9 (
    .D(DATA_WRITE_2), .en(demultiplexer_2_out0), .Q(register_9_q), .clk(CLK), .clr(RESET));
  Register #(.width(32)) register_10 (
    .D(DATA_WRITE_2), .en(demultiplexer_2_out1), .Q(register_10_q), .clk(CLK), .clr(RESET));
  Register #(.width(32)) register_11 (
    .D(DATA_WRITE_2), .en(demultiplexer_2_out2), .Q(register_11_q), .clk(CLK), .clr(RESET));
  Register #(.width(32)) register_12 (
    .D(DATA_WRITE_2), .en(demultiplexer_2_out3), .Q(register_12_q), .clk(CLK), .clr(RESET));
  Register #(.width(32)) register_13 (
    .D(DATA_WRITE_2), .en(demultiplexer_2_out4), .Q(register_13_q), .clk(CLK), .clr(RESET));
  Register #(.width(32)) register_14 (
    .D(DATA_WRITE_2), .en(demultiplexer_2_out5), .Q(register_14_q), .clk(CLK), .clr(RESET));
  Register #(.width(32)) register_15 (
    .D(DATA_WRITE_2), .en(demultiplexer_2_out6), .Q(register_15_q), .clk(CLK), .clr(RESET));
  Register #(.width(32)) register_16 (
    .D(DATA_WRITE_2), .en(demultiplexer_2_out7), .Q(register_16_q), .clk(CLK), .clr(RESET));
  Multiplexer #(.select(4), .width(32), .disabled(0), .enable("false")) multiplexer_1 (
    .in0(register_1_q), .in1(register_2_q), .in2(register_3_q), .in3(register_4_q), .in4(register_5_q),
    .in5(register_6_q), .in6(register_7_q), .in7(register_8_q), .in8(register_9_q), .in9(register_10_q),
    .in10(register_11_q), .in11(register_12_q), .in12(register_13_q), .in13(register_14_q),
    .in14(register_15_q), .in15(register_16_q), .out(R0_D), .sel(R0));
  Multiplexer #(.select(4), .width(32), .enable("false")) multiplexer_2 (
    .in0(register_1_q), .in1(register_2_q), .in2(register_3_q), .in3(register_4_q), .in4(register_5_q),
    .in5(register_6_q), .in6(register_7_q), .in7(register_8_q), .in8(register_9_q), .in9(register_10_q),
    .in10(register_11_q), .in11(register_12_q), .in12(register_13_q), .in13(register_14_q),
    .in14(register_15_q), .in15(register_16_q), .out(R1_D), .sel(R1));
  Multiplexer #(.select(4), .width(32), .enable("false")) multiplexer_3 (
    .in0(register_1_q), .in1(register_2_q), .in2(register_3_q), .in3(register_4_q), .in4(register_5_q),
    .in5(register_6_q), .in6(register_7_q), .in7(register_8_q), .in8(register_9_q), .in9(register_10_q),
    .in10(register_11_q), .in11(register_12_q), .in12(register_13_q), .in13(register_14_q),
    .in14(register_15_q), .in15(register_16_q), .out(R2_D), .sel(R2));
  Multiplexer #(.select(4), .width(32), .enable("false")) multiplexer_4 (
    .in0(register_1_q), .in1(register_2_q), .in2(register_3_q), .in3(register_4_q), .in4(register_5_q),
    .in5(register_6_q), .in6(register_7_q), .in7(register_8_q), .in8(register_9_q), .in9(register_10_q),
    .in10(register_11_q), .in11(register_12_q), .in12(register_13_q), .in13(register_14_q),
    .in14(register_15_q), .in15(register_16_q), .out(R3_D), .sel(R3));

  // Other names for the same wires on the sheet: In[31:0] = DATA_WRITE; In_2[31:0] = DATA_WRITE_2; R = RESET
endmodule

// auxiliar
module auxiliar_do_branch (
  input  [31:0] Normal,
  input  [31:0] Sem_soma,
  input  in_3,
  input  j,
  output [31:0] out_5
);

  wire [31:0] adder_1_out, multiplexer_1_out;

  Adder #(.width(32)) adder_1 (
    .a({{9{1'b0}}, Sem_soma[20:0], 2'b00}), .b(Normal), .out(adder_1_out));  // open: cin, cout
  Multiplexer #(.width(32), .enable("false")) multiplexer_1 (
    .in0(Normal), .in1(adder_1_out), .out(multiplexer_1_out), .sel(in_3));
  Multiplexer #(.width(32), .enable("false")) multiplexer_2 (
    .in0(multiplexer_1_out), .in1({2'b00, Sem_soma[27:0], 2'b00}), .out(out_5), .sel(j));
endmodule

// Data Memory
module MemoriaDados (
  input  [31:0] in_1,
  input  MemRead,
  input  [31:0] in_3,
  input  clk,
  input  MemWrite,
  input  limpa,
  output [31:0] out_7
);

  wire [31:0] ram_1_data;

  RAM #(.addrWidth(24), .dataWidth(32), .bus("separate")) ram_1 (
    .addr(in_1[23:0]), .din(in_3), .data(ram_1_data), .str(MemWrite), .clk(clk), .clr(limpa));  // open: sel, ld
  Multiplexer #(.width(32), .enable("false")) multiplexer_1 (.in0(in_1), .in1(ram_1_data), .out(out_7), .sel(MemRead));
endmodule

module REDUTOR (
  input  [31:0] in_1,
  output [31:0] out_2
);


  assign out_2 = {{8{1'b0}}, in_1[23:0]};
endmodule

module Pipeline_1 (
  input  [31:0] in_1,
  input  [31:0] in_2,
  input  [31:0] in_3,
  input  in_4,
  input  in_5,
  output [31:0] out_6,
  output [31:0] out_7,
  output [31:0] out_8
);

  Register #(.width(32)) register_1 (.D(in_1), .Q(out_6), .clk(in_4), .clr(in_5));  // open: en
  Register #(.width(32)) register_2 (.D(in_2), .Q(out_7), .clk(in_4), .clr(in_5));  // open: en
  Register #(.width(32)) register_3 (.D(in_3), .Q(out_8), .clk(in_4), .clr(in_5));  // open: en
endmodule

module Pipeline_2 (
  input  [15:0] in_1,
  input  [31:0] in_2,
  input  [31:0] in_3,
  input  [31:0] in_4,
  input  [31:0] in_5,
  input  [5:0] in_6,
  input  in_7,
  input  in_8,
  output [15:0] out_9,
  output [31:0] out_10,
  output [31:0] out_11,
  output [31:0] out_12,
  output [31:0] out_13,
  output [5:0] out_14
);

  Register #(.width(16)) register_1 (.D(in_1), .Q(out_9), .clk(in_7), .clr(in_8));  // open: en
  Register #(.width(32)) register_2 (.D(in_2), .Q(out_10), .clk(in_7), .clr(in_8));  // open: en
  Register #(.width(32)) register_3 (.D(in_3), .Q(out_11), .clk(in_7), .clr(in_8));  // open: en
  Register #(.width(32)) register_4 (.D(in_4), .Q(out_12), .clk(in_7), .clr(in_8));  // open: en
  Register #(.width(32)) register_5 (.D(in_5), .Q(out_13), .clk(in_7), .clr(in_8));  // open: en
  Register #(.width(6)) register_6 (.D(in_6), .Q(out_14), .clk(in_7), .clr(in_8));  // open: en
endmodule

module Pipeline_3 (
  input  [5:0] in_1,
  input  [31:0] in_2,
  input  [31:0] in_3,
  input  [31:0] in_4,
  input  [31:0] in_5,
  input  [31:0] in_6,
  input  [5:0] in_7,
  input  in_8,
  input  in_9,
  input  in_10,
  output [5:0] out_11,
  output [31:0] out_12,
  output [31:0] out_13,
  output [31:0] out_14,
  output [31:0] out_15,
  output [31:0] out_16,
  output [5:0] out_17,
  output out_18
);

  Register #(.width(6)) register_1 (.D(in_1), .Q(out_11), .clk(in_9), .clr(in_10));  // open: en
  Register #(.width(32)) register_2 (.D(in_2), .Q(out_12), .clk(in_9), .clr(in_10));  // open: en
  Register #(.width(32)) register_3 (.D(in_3), .Q(out_13), .clk(in_9), .clr(in_10));  // open: en
  Register #(.width(32)) register_4 (.D(in_4), .Q(out_14), .clk(in_9), .clr(in_10));  // open: en
  Register #(.width(32)) register_5 (.D(in_5), .Q(out_15), .clk(in_9), .clr(in_10));  // open: en
  Register #(.width(32)) register_6 (.D(in_6), .Q(out_16), .clk(in_9), .clr(in_10));  // open: en
  Register #(.width(6)) register_7 (.D(in_7), .Q(out_17), .clk(in_9), .clr(in_10));  // open: en
  Register #(.width(1)) register_8 (.D(in_8), .Q(out_18), .clk(in_9), .clr(in_10));  // open: en
endmodule

module Pipeline_4 (
  input  [3:0] in_1,
  input  [31:0] in_2,
  input  [31:0] in_3,
  input  [5:0] in_4,
  input  in_5,
  input  in_6,
  output [3:0] out_7,
  output [31:0] out_8,
  output [31:0] out_9,
  output [5:0] out_10
);

  Register #(.width(4)) register_1 (.D(in_1), .Q(out_7), .clk(in_5), .clr(in_6));  // open: en
  Register #(.width(32)) register_2 (.D(in_2), .Q(out_8), .clk(in_5), .clr(in_6));  // open: en
  Register #(.width(32)) register_3 (.D(in_3), .Q(out_9), .clk(in_5), .clr(in_6));  // open: en
  Register #(.width(6)) register_4 (.D(in_4), .Q(out_10), .clk(in_5), .clr(in_6));  // open: en
endmodule

module MemoriaInstrucoes (
  input  [7:0] in_1,
  output [31:0] out_2,
  output [31:0] out_3
);

  ROM #(.dataWidth(32)) rom_1 (.addr(in_1), .data(out_2));  // open: sel
  ROM #(.dataWidth(32)) rom_2 (.addr(in_1), .data(out_3));  // open: sel

  // Notes on the sheet:
  //   contents of rom_1 (hex, n*v repeats v):
  //   20000004 21000001 22000010 b0000000 60800013 4*b0000000 600d0009 b0000000 a4000000 45080000 c5900000
  //   c5d00000 f0400000 b0000000 b0000000 30000009 90bc0000 b0000000 b0000000 b0000000 30000004 5*b0000000
  //   60f00024 4*b0000000 60b00019 4*b0000000 60c0000d 430f0000 c3c00000 c3900000 e3000000 b0000000
  //   b0000000 b0000000 840e0000 4*b0000000 30000027 b0000000 b0000000 430f0000 c3b00000 c3a00000 f0d00000
  //   30000022 4*b0000000 3000001d 4*b0000000
  //   contents of rom_2 (hex, n*v repeats v):
  //   20000000 21000000 22000020 b0000000 25000000 6*b0000000 ab000000 44080000 c4200000 c4d00000 b0000000
  //   51d0000 6*b0000000 180000 27000000 4*b0000000 23000000 4*b0000000 24000000 b0000000 b0000000
  //   b0000000 25000000 b0000000 460c0000 c6b00000 c6200000 4*b0000000 41c0000 4*b0000000 46340000
  //   c5d00000 b0000000 b0000000 b0000000 31b0000 5*b0000000 71f0000 5*b0000000
endmodule
