// Logisim project mips-like_ciclico.circ as structural Verilog: 6 circuits, main circuit UC
module PROCESSADOR (
  output [31:0] \INSTRUÇÃO 
);

  wire and_1_out, branch, button_1_out, clock_1_out, j, mine_out, T_or_F, UC_li, UC_memread, UC_memwrite,
       UC_write_reg;
  wire [1:0] UC_ula_op;
  wire [31:0] adder_1_out, auxiliar_do_branch_1_out_5, banco_de_registradores_1_r0_d,
       banco_de_registradores_1_r1_d, data_memory_1_out_6, multiplexer_1_out, multiplexer_2_out,
       multiplexer_3_out, PC_q, ula_1_ula_out;

  Adder #(.width(32)) adder_1 (.a(PC_q), .b(32'h4), .out(adder_1_out));  // open: cin, cout
  auxiliar_do_branch auxiliar_do_branch_1 (
    .Normal(adder_1_out), .Sem_soma(PC_q), .Valor_adicionado(\INSTRUÇÃO [19:0]), .in_3(and_1_out),
    .out_5(auxiliar_do_branch_1_out_5));
  and and_1 (and_1_out, branch, T_or_F);
  Multiplexer #(.width(32), .enable("false")) multiplexer_1 (
    .in0(auxiliar_do_branch_1_out_5), .in1({2'b00, \INSTRUÇÃO [27:0], 2'b00}), .out(multiplexer_1_out),
    .sel(j));
  Clock clock_1 (.out(clock_1_out));
  Register #(.width(32)) PC (.D(multiplexer_1_out), .Q(PC_q), .clk(clock_1_out), .clr(button_1_out));  // open: en
  Button button_1 (.out(button_1_out));
  ROM #(.dataWidth(32)) rom_1 (.addr(PC_q[9:2]), .data(\INSTRUÇÃO ));  // open: sel
  UC UC (
    .E3(\INSTRUÇÃO [31]), .E2(\INSTRUÇÃO [30]), .E1(\INSTRUÇÃO [29]), .ula_op(UC_ula_op[0]),
    .E0(\INSTRUÇÃO [28]), .ula_r(UC_ula_op[1]), .write_reg(UC_write_reg), .li(UC_li), .j(j), .branch(branch),
    .MemRead(UC_memread), .MemWrite(UC_memwrite));
  BANCO_DE_REGISTRADORES banco_de_registradores_1 (
    .DATA_WRITE(multiplexer_2_out), .CLK(clock_1_out), .RW(\INSTRUÇÃO [27:24]),
    .R0_D(banco_de_registradores_1_r0_d), .R0(\INSTRUÇÃO [19:16]), .R1_D(banco_de_registradores_1_r1_d),
    .R1(\INSTRUÇÃO [23:20]), .RW_2(UC_write_reg), .RESET(button_1_out));
  Multiplexer #(.width(32), .enable("false")) multiplexer_2 (
    .in0(data_memory_1_out_6), .in1({{8{1'b0}}, \INSTRUÇÃO [23:0]}), .out(multiplexer_2_out), .sel(UC_li));
  ULA ula_1 (
    .DATA_0(banco_de_registradores_1_r0_d), .DATA_1(banco_de_registradores_1_r1_d), .ULA_OUT(ula_1_ula_out),
    .ULA_OP(UC_ula_op), .out_6(T_or_F), .clk(clock_1_out));
  Multiplexer #(.width(32), .enable("false")) multiplexer_3 (
    .in0(ula_1_ula_out), .in1(banco_de_registradores_1_r0_d), .out(multiplexer_3_out), .sel(mine_out));
  or mine (mine_out, UC_memwrite, UC_memread);
  data_memory data_memory_1 (
    .in_1(multiplexer_3_out), .in_3(banco_de_registradores_1_r1_d), .MemWrite(UC_memwrite),
    .out_6(data_memory_1_out_6), .clk(clock_1_out), .MemRead(UC_memread));

  // Notes on the sheet:
  //   REG_0
  //   REG_1
  //   REG_W
  //   contents of rom_1 (hex, n*v repeats v):
  //   20000007 90000000 81000000 a0000000
  //   DATA_W
  //   BANCO DE REGISTRADORES
  //   REG0_D
  //   REG1_D
  //   ULA
endmodule

module ULA (
  input  [31:0] DATA_0,
  input  [31:0] DATA_1,
  input  [1:0] ULA_OP,
  input  clk,
  output [31:0] ULA_OUT,
  output out_6
);

  wire comparator_1_eq, comparator_1_gt, comparator_1_lt;
  wire [6:0] random_1_out;
  wire [31:0] adder_1_out, multiplier_1_out, subtractor_1_out;

  Adder #(.width(32)) adder_1 (.a(DATA_0), .b(DATA_1), .out(adder_1_out));  // open: cin, cout
  Subtractor #(.width(32)) subtractor_1 (.a(DATA_0), .b(DATA_1), .out(subtractor_1_out));  // open: bin, bout
  Multiplier #(.width(32)) multiplier_1 (.a(DATA_0), .b(DATA_1), .out(multiplier_1_out));  // open: cin, cout
  Comparator #(.width(32), .mode("unsigned")) comparator_1 (
    .a(DATA_0), .b(DATA_1), .gt(comparator_1_gt), .eq(comparator_1_eq), .lt(comparator_1_lt));
  Random #(.width(7)) random_1 (.clk(clk), .out(random_1_out));  // open: next, clr
  Multiplexer #(.select(2), .width(32), .enable("false")) multiplexer_1 (
    .in0(adder_1_out), .in1(subtractor_1_out), .in2(multiplier_1_out), .in3({random_1_out, {25{1'b0}}}),
    .out(ULA_OUT), .sel(ULA_OP));
  Multiplexer #(.select(2), .enable("false")) multiplexer_2 (
    .in0(comparator_1_gt), .in1(comparator_1_eq), .in2(comparator_1_lt), .in3(1'b0), .out(out_6), .sel(ULA_OP));
endmodule

module UC (
  input  E3,
  input  E2,
  input  E1,
  input  E0,
  output ula_op,
  output ula_r,
  output write_reg,
  output li,
  output j,
  output branch,
  output MemRead,
  output MemWrite
);

  wire and_1_out, and_2_out, and_3_out, and_4_out, and_5_out, and_6_out, and_7_out, and_8_out, and_9_out,
       and_10_out, and_11_out, not_1_out, not_2_out, not_3_out, not_4_out, not_5_out, not_6_out, not_7_out,
       not_8_out, not_9_out, not_10_out, not_11_out, not_12_out, not_13_out, not_14_out, not_15_out,
       not_16_out, not_17_out, not_18_out, not_19_out, not_20_out, not_21_out, not_22_out, not_23_out,
       not_24_out, not_25_out, not_26_out, not_27_out, not_28_out;

  not not_1 (not_1_out, E2);
  not not_2 (not_2_out, E1);
  not not_3 (not_3_out, E3);
  not not_4 (not_4_out, E0);
  not not_5 (not_5_out, E2);
  not not_6 (not_6_out, E3);
  not not_7 (not_7_out, E1);
  not not_8 (not_8_out, E0);
  not not_9 (not_9_out, E3);
  not not_10 (not_10_out, E2);
  not not_11 (not_11_out, E0);
  not not_12 (not_12_out, E3);
  not not_13 (not_13_out, E2);
  and and_1 (and_1_out, not_12_out, not_13_out, not_14_out);
  not not_14 (not_14_out, E1);
  not not_15 (not_15_out, E2);
  and and_2 (and_2_out, not_15_out, not_16_out);
  not not_16 (not_16_out, E0);
  not not_17 (not_17_out, E3);
  not not_18 (not_18_out, E2);
  not not_19 (not_19_out, E0);
  not not_20 (not_20_out, E3);
  not not_21 (not_21_out, E2);
  not not_22 (not_22_out, E3);
  and and_3 (and_3_out, not_22_out, E2, E0);
  not not_23 (not_23_out, E3);
  and and_4 (and_4_out, not_23_out, E2, E1);
  not not_24 (not_24_out, E2);
  not not_25 (not_25_out, E1);
  not not_26 (not_26_out, E0);
  not not_27 (not_27_out, E2);
  not not_28 (not_28_out, E1);
  and and_5 (and_5_out, not_1_out, not_2_out, E0);
  and and_6 (and_6_out, not_3_out, E2, E1, not_4_out);
  and and_7 (and_7_out, E3, E0);
  and and_8 (and_8_out, E3, not_5_out, E1);
  and and_9 (and_9_out, not_6_out, E2, not_7_out, not_8_out);
  or or_1 (ula_r, and_9_out, and_10_out, and_11_out);
  and and_10 (and_10_out, not_9_out, E2, E1, E0);
  and and_11 (and_11_out, E3, not_10_out, E1, not_11_out);
  or or_2 (write_reg, and_1_out, and_2_out);
  and and_12 (li, not_17_out, not_18_out, E1, not_19_out);
  and and_13 (j, not_20_out, not_21_out, E1, E0);
  or or_3 (branch, and_3_out, and_4_out);
  and and_14 (MemRead, E3, not_24_out, not_25_out, not_26_out);
  and and_15 (MemWrite, E3, not_27_out, not_28_out, E0);
  or or_4 (ula_op, and_5_out, and_6_out, and_7_out, and_8_out);
endmodule

module BANCO_DE_REGISTRADORES (
  input  [31:0] DATA_WRITE,
  input  [3:0] R0,
  input  [3:0] R1,
  input  [3:0] RW,
  input  CLK,
  input  RESET,
  input  RW_2,
  output [31:0] R0_D,
  output [31:0] R1_D
);

  wire demultiplexer_1_out0, demultiplexer_1_out1, demultiplexer_1_out2, demultiplexer_1_out3,
       demultiplexer_1_out4, demultiplexer_1_out5, demultiplexer_1_out6, demultiplexer_1_out7,
       demultiplexer_1_out8, demultiplexer_1_out9, demultiplexer_1_out10, demultiplexer_1_out11,
       demultiplexer_1_out12, demultiplexer_1_out13, demultiplexer_1_out14, demultiplexer_1_out15;
  wire [31:0] register_1_q, register_2_q, register_3_q, register_4_q, register_5_q, register_6_q,
       register_7_q, register_8_q, register_9_q, register_10_q, register_11_q, register_12_q, register_13_q,
       register_14_q, register_15_q, register_16_q;

  Demultiplexer #(.select(4)) demultiplexer_1 (
    .out0(demultiplexer_1_out0), .out1(demultiplexer_1_out1), .out2(demultiplexer_1_out2),
    .out3(demultiplexer_1_out3), .out4(demultiplexer_1_out4), .out5(demultiplexer_1_out5),
    .out6(demultiplexer_1_out6), .out7(demultiplexer_1_out7), .out8(demultiplexer_1_out8),
    .out9(demultiplexer_1_out9), .out10(demultiplexer_1_out10), .out11(demultiplexer_1_out11),
    .out12(demultiplexer_1_out12), .out13(demultiplexer_1_out13), .out14(demultiplexer_1_out14),
    .out15(demultiplexer_1_out15), .in(RW_2), .sel(RW));  // open: en
  Register #(.width(32)) register_1 (
    .D(DATA_WRITE), .en(demultiplexer_1_out0), .Q(register_1_q), .clk(CLK), .clr(RESET));
  Register #(.width(32)) register_2 (
    .D(DATA_WRITE), .en(demultiplexer_1_out1), .Q(register_2_q), .clk(CLK), .clr(RESET));
  Register #(.width(32)) register_3 (
    .D(DATA_WRITE), .en(demultiplexer_1_out2), .Q(register_3_q), .clk(CLK), .clr(RESET));
  Register #(.width(32)) register_4 (
    .D(DATA_WRITE), .en(demultiplexer_1_out3), .Q(register_4_q), .clk(CLK), .clr(RESET));
  Register #(.width(32)) register_5 (
    .D(DATA_WRITE), .en(demultiplexer_1_out4), .Q(register_5_q), .clk(CLK), .clr(RESET));
  Register #(.width(32)) register_6 (
    .D(DATA_WRITE), .en(demultiplexer_1_out5), .Q(register_6_q), .clk(CLK), .clr(RESET));
  Register #(.width(32)) register_7 (
    .D(DATA_WRITE), .en(demultiplexer_1_out6), .Q(register_7_q), .clk(CLK), .clr(RESET));
  Register #(.width(32)) register_8 (
    .D(DATA_WRITE), .en(demultiplexer_1_out7), .Q(register_8_q), .clk(CLK), .clr(RESET));
  Register #(.width(32)) register_9 (
    .D(DATA_WRITE), .en(demultiplexer_1_out8), .Q(register_9_q), .clk(CLK), .clr(RESET));
  Register #(.width(32)) register_10 (
    .D(DATA_WRITE), .en(demultiplexer_1_out9), .Q(register_10_q), .clk(CLK), .clr(RESET));
  Register #(.width(32)) register_11 (
    .D(DATA_WRITE), .en(demultiplexer_1_out10), .Q(register_11_q), .clk(CLK), .clr(RESET));
  Register #(.width(32)) register_12 (
    .D(DATA_WRITE), .en(demultiplexer_1_out11), .Q(register_12_q), .clk(CLK), .clr(RESET));
  Register #(.width(32)) register_13 (
    .D(DATA_WRITE), .en(demultiplexer_1_out12), .Q(register_13_q), .clk(CLK), .clr(RESET));
  Register #(.width(32)) register_14 (
    .D(DATA_WRITE), .en(demultiplexer_1_out13), .Q(register_14_q), .clk(CLK), .clr(RESET));
  Register #(.width(32)) register_15 (
    .D(DATA_WRITE), .en(demultiplexer_1_out14), .Q(register_15_q), .clk(CLK), .clr(RESET));
  Register #(.width(32)) register_16 (
    .D(DATA_WRITE), .en(demultiplexer_1_out15), .Q(register_16_q), .clk(CLK), .clr(RESET));
  Multiplexer #(.select(4), .width(32), .disabled(0), .enable("false")) multiplexer_1 (
    .in0(register_1_q), .in1(register_2_q), .in2(register_3_q), .in3(register_4_q), .in4(register_5_q),
    .in5(register_6_q), .in6(register_7_q), .in7(register_8_q), .in8(register_9_q), .in9(register_10_q),
    .in10(register_11_q), .in11(register_12_q), .in12(register_13_q), .in13(register_14_q),
    .in14(register_15_q), .in15(register_16_q), .out(R0_D), .sel(R0));
  Multiplexer #(.select(4), .width(32), .enable("false")) multiplexer_2 (
    .in0(register_1_q), .in1(register_2_q), .in2(register_3_q), .in3(register_4_q), .in4(register_5_q),
    .in5(register_6_q), .in6(register_7_q), .in7(register_8_q), .in8(register_9_q), .in9(register_10_q),
    .in10(register_11_q), .in11(register_12_q), .in12(register_13_q), .in13(register_14_q),
    .in14(register_15_q), .in15(register_16_q), .out(R1_D), .sel(R1));

  // Other names for the same wires on the sheet: In[31:0] = DATA_WRITE; R = RESET
endmodule

// auxiliar
module auxiliar_do_branch (
  input  [31:0] Normal,
  input  [31:0] Sem_soma,
  input  in_3,
  input  [19:0] Valor_adicionado,
  output [31:0] out_5
);

  wire [31:0] adder_1_out;

  Adder #(.width(32)) adder_1 (
    .a(Sem_soma), .b({{10{1'b0}}, Valor_adicionado, 2'b00}), .out(adder_1_out));  // open: cin, cout
  Multiplexer #(.width(32), .enable("false")) multiplexer_1 (.in0(Normal), .in1(adder_1_out), .out(out_5), .sel(in_3));
endmodule

// Data Memory
module data_memory (
  input  [31:0] in_1,
  input  MemRead,
  input  [31:0] in_3,
  input  clk,
  input  MemWrite,
  output [31:0] out_6
);

  wire [31:0] ram_1_data;

  RAM #(.addrWidth(24), .dataWidth(32), .bus("separate")) ram_1 (
    .addr(in_1[23:0]), .din(in_3), .data(ram_1_data), .str(MemWrite), .clk(clk));  // open: sel, ld, clr
  Multiplexer #(.width(32), .enable("false")) multiplexer_1 (.in0(in_1), .in1(ram_1_data), .out(out_6), .sel(MemRead));
endmodule
